# Fritzing sketch Paddle_of_Theseus (saved by Fritzing 0.9.3b)
breadboards: 1

parts:
  Capacitive_Touch_Sensor0 = Adafruit AT42QT1010 Standalone Momentary Capacitive Touch Sensor [part_number=Capacitive_Touch_Sensor]
  Microcontroller = Teensy 3.1
  R5 = Resistor [tolerance=±5% resistance=1k package=THT]
  Linear_Potentiometer = SoftPot Membrane Potentiometer - 50mm [part_number=SEN-08680]
  Illuminated_RGB_Rot_Enc = ENCODER_RGB_CA [package=encoder_led_3]
  R6 = Resistor [tolerance=±5% resistance=10k package=THT]
  3-Axis_Accelerometer = 3-Axis Accelerometer Breakout - MMA8452Q
  US-100/_RCWL-1601/_Ping = US-100 Ultrasonic Rangefinder
  Capacitive_Touch_Sensor1 = Adafruit AT42QT1010 Standalone Momentary Capacitive Touch Sensor [part_number=Capacitive_Touch_Sensor]
  Capacitive_Touch_Sensor2 = Adafruit AT42QT1010 Standalone Momentary Capacitive Touch Sensor [part_number=Capacitive_Touch_Sensor]
  Capacitive_Touch_Sensor3 = Adafruit AT42QT1010 Standalone Momentary Capacitive Touch Sensor [part_number=Capacitive_Touch_Sensor]
  Rotary_Potentiometer = Rotary Potentiometer (Small) [maximum_resistance=100kΩ package=THT]
  R9 = Resistor [tolerance=±5% resistance=1k package=THT]

nets:
  3V3: Capacitive_Touch_Sensor0.VDD, Microcontroller.3V3, Linear_Potentiometer.leg1, Illuminated_RGB_Rot_Enc.+, 3-Axis_Accelerometer.3.3V, US-100/_RCWL-1601/_Ping.VCC, Capacitive_Touch_Sensor1.VDD, Capacitive_Touch_Sensor2.VDD, Capacitive_Touch_Sensor3.VDD, Rotary_Potentiometer.leg1
  TEENSY_CAP_TOUCH_0_PIN: Capacitive_Touch_Sensor0.OUT, Microcontroller.D10
  GND: Capacitive_Touch_Sensor0.GND, Microcontroller.GND, R5.Pin_1, Linear_Potentiometer.leg2, Illuminated_RGB_Rot_Enc.C, R6.Pin_0, 3-Axis_Accelerometer.GND, US-100/_RCWL-1601/_Ping.GND, US-100/_RCWL-1601/_Ping.GND*, Capacitive_Touch_Sensor1.GND, Capacitive_Touch_Sensor2.GND, Capacitive_Touch_Sensor3.GND, Rotary_Potentiometer.leg2, R9.Pin_1
  TEENSY_RGB_R_PIN: Microcontroller.D1, Illuminated_RGB_Rot_Enc.-R
  TEENSY_RGB_G_PIN: Microcontroller.D2, Illuminated_RGB_Rot_Enc.-G
  TEENSY_ROT_ENC_BUTTON_PIN: Microcontroller.D3, Illuminated_RGB_Rot_Enc.SW, R6.Pin_1
  TEENSY_RGB_B_PIN: Microcontroller.D4, Illuminated_RGB_Rot_Enc.-B
  TEENSY_ROT_ENC_CLK_PIN: Microcontroller.D5, Illuminated_RGB_Rot_Enc.B
  TEENSY_ROT_ENC_DT_PIN: Microcontroller.D6, Illuminated_RGB_Rot_Enc.A
  TEENSY_CAP_TOUCH_3_PIN: Microcontroller.D7, Capacitive_Touch_Sensor3.OUT
  TEENSY_CAP_TOUCH_2_PIN: Microcontroller.D8, Capacitive_Touch_Sensor2.OUT
  TEENSY_CAP_TOUCH_1_PIN: Microcontroller.D9, Capacitive_Touch_Sensor1.OUT
  TEENSY_ULTRASONIC_TRIG_PIN: Microcontroller.D11, US-100/_RCWL-1601/_Ping.Trig/Tx
  TEENSY_ULTRASONIC_SENS_PIN: Microcontroller.D12, US-100/_RCWL-1601/_Ping.Echo/Rx
  TEENSY_LIN_POT_PIN: Microcontroller.A0/D14, R5.Pin_0, Linear_Potentiometer.wiper
  TEENSY_ROT_POT_PIN: Microcontroller.A1/D15, Rotary_Potentiometer.wiper, R9.Pin_0
  TEENSY_SDA_PIN: Microcontroller.A4/D18, 3-Axis_Accelerometer.SDA
  TEENSY_SCL_PIN: Microcontroller.A5/D19, 3-Axis_Accelerometer.SCL

notes:
  Paddle of Theseus, All systems of the Paddle of Theseus - NOTE: These are all breakout boards, there is NO PCB layout file, 1.0
  SpectraSymbol ThinPot
  Adafruit AT42QT1010
  SparkFun SEN-12756
  SparkFun COM-15141 Illum Rot Enc
  Teensy 4.0/ Teensy LC
  NOTE: For Parallax Ping, only use pin 12 (TEENSY_ULTRA_SENS_PIN) into single Ping I/O pin
  Rotary Potentiometer

custom parts:
  Adafruit AT42QT1010 Standalone Momentary Capacitive Touch Sensor: This breakout board is the simplest way to create a project with a single "momentary" capacitive touch sensor. No microcontroller is required here - just power with 1.8 to 5.5VDC and touch the pad to activate the sensor. When a capacitive load is detected (e.g. a person touches the sensor-pad area) the red LED lights up and the output pin goes high. You can also solder a wire to the middle pad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
  SoftPot Membrane Potentiometer - 50mm: These are very thin variable potentiometers. By pressing down on various parts of the strip, the resistance linearly changes from 100Ohms to 10,000Ohms allowing the user to very accurately calculate the relative position on the strip. Can be used as an accurate positional indicator for CNC head positioning, variable user input (volume level input for example), straight user input (multiple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
